// Logisim project simcomputer.circ as structural Verilog: 25 circuits, main circuit sysboard
module sysboard (
);

  wire button_1_out, button_2_out, button_3_out, clock_1_clk, clock_1_pclk, clock_1_status, cpu_1602_1_io_se,
       cpu_1602_1_out_7, cpu_1602_1_out_12, cpu_1602_1_out_13, cpu_1602_1_pgm_data, panel_1_out_8,
       panel_1_out_9, panel_1_out_10, panel_1_out_11, panel_1_out_12, panel_1_out_13, panel_1_out_14,
       tc7_1_clear, tc7_1_clk_out, tc7_1_enbl_2;
  wire [6:0] tc7_1_data_out;
  wire [7:0] cpu_1602_1_stack_store;
  wire [15:0] addrstack_1_out_6, cpu_1602_1_out_8, cpu_1602_1_out_9, cpu_1602_1_out_10, cpu_1602_1_out_11,
       cpu_1602_1_stack_load, ram_1_out_6, romchip_1_out_2;

  TTY #(.rows(15), .cols(60)) tty_1 (.data(tc7_1_data_out), .clk(tc7_1_clk_out), .we(tc7_1_enbl_2), .clr(tc7_1_clear));
  clock clock_1 (
    .RUN(panel_1_out_12), .BREAK(panel_1_out_13), .RESET(panel_1_out_14), .STATUS(clock_1_status),
    .CLK(clock_1_clk), .PCLK(clock_1_pclk));
  romchip romchip_1 (.in_1(cpu_1602_1_out_11), .out_2(romchip_1_out_2));
  tc7 tc7_1 (
    .CLK_IN(clock_1_clk), .DATA_OUT(tc7_1_data_out), .CLK_OUT(tc7_1_clk_out), .ENBL_2(tc7_1_enbl_2),
    .CLEAR(tc7_1_clear), .in_2(cpu_1602_1_out_10), .ENBL(cpu_1602_1_out_7), .RESET(panel_1_out_14));
  cpu_1602 cpu_1602_1 (
    .out_7(cpu_1602_1_out_7), .RST(panel_1_out_14), .IO_SE(cpu_1602_1_io_se), .CLK(clock_1_clk),
    .in_3(addrstack_1_out_6), .stack_load(cpu_1602_1_stack_load), .out_8(cpu_1602_1_out_8),
    .in_1(ram_1_out_6), .out_9(cpu_1602_1_out_9), .out_10(cpu_1602_1_out_10), .out_11(cpu_1602_1_out_11),
    .pgm_address(romchip_1_out_2), .stack_store(cpu_1602_1_stack_store), .out_12(cpu_1602_1_out_12),
    .out_13(cpu_1602_1_out_13), .pgm_data(cpu_1602_1_pgm_data));
  ram ram_1 (
    .in_1(clock_1_clk), .in_2(cpu_1602_1_out_8), .out_6(ram_1_out_6), .in_3(cpu_1602_1_out_9),
    .in_4(cpu_1602_1_io_se), .in_5(panel_1_out_14));
  addrstack addrstack_1 (
    .in_1(cpu_1602_1_stack_store), .in_2(cpu_1602_1_stack_load), .out_6(addrstack_1_out_6),
    .in_3(cpu_1602_1_pgm_data), .in_4(clock_1_clk), .in_5(panel_1_out_14));
  Button button_1 (.out(button_1_out));
  LED led_1 (.in(panel_1_out_8));
  Button button_2 (.out(button_2_out));
  panel panel_1 (
    .in_1(button_1_out), .out_8(panel_1_out_8), .in_2(button_2_out), .in_3(button_3_out),
    .out_9(panel_1_out_9), .out_10(panel_1_out_10), .out_11(panel_1_out_11), .in_4(cpu_1602_1_out_12),
    .in_5(cpu_1602_1_out_13), .out_12(panel_1_out_12), .out_13(panel_1_out_13), .out_14(panel_1_out_14),
    .in_6(clock_1_status), .in_7(clock_1_pclk));
  Button button_3 (.out(button_3_out));
  LED led_2 (.in(panel_1_out_9));
  LED led_3 (.in(panel_1_out_10));
  LED led_4 (.in(panel_1_out_11));

  // Notes on the sheet:
  //   (C) Copyright 2013, 2014 R. Altnoeder
  //   (CC)(by)(sa)(nc) - Creative Commons attribution, share-alike, noncommercial license | Release: 2014-01-03
endmodule

module instr_copy (
  input  [15:0] in_1,
  input  [15:0] in_2,
  output [15:0] out_3
);


  assign out_3 = in_1;
endmodule

module instr_lflg (
  input  [15:0] in_1,
  input  [15:0] in_2,
  input  [7:0] in_3,
  output [15:0] out_4
);


  assign out_4 = {{8{1'b0}}, in_3};
endmodule

module addrstack (
  input  [7:0] in_1,
  input  [15:0] in_2,
  input  in_3,
  input  in_4,
  input  in_5,
  output [15:0] out_6
);

  wire not_1_out;

  Pull_Resistor pull_resistor_1 (.node(in_5));
  Pull_Resistor pull_resistor_2 (.node(in_3));
  not not_1 (not_1_out, in_3);
  RAM #(.dataWidth(16), .bus("separate")) ram_1 (
    .addr(in_1), .din(in_2), .data(out_6), .str(in_3), .sel(1'b1), .clk(in_4), .ld(not_1_out), .clr(in_5));
endmodule

module clock (
  input  RUN,
  input  BREAK,
  input  RESET,
  output STATUS,
  output CLK,
  output PCLK
);

  wire or_1_out, t_ff_1_q;

  T_Flip_Flop t_ff_1 (.Q(t_ff_1_q), .preset(RUN), .reset(or_1_out));  // open: clk, T, Qn, en
  or or_1 (or_1_out, BREAK, RESET);
  D_Flip_Flop #(.trigger("falling")) d_ff_1 (
    .clk(PCLK), .D(t_ff_1_q), .Q(STATUS), .en(1'b1), .reset(RESET));  // open: Qn, preset
  Clock clock_1 (.out(PCLK));
  and and_1 (CLK, STATUS, PCLK);
endmodule

module ram (
  input  in_1,
  input  [15:0] in_2,
  input  [15:0] in_3,
  input  in_4,
  input  in_5,
  output [15:0] out_6
);

  wire not_1_out;

  not not_1 (not_1_out, in_4);
  RAM #(.addrWidth(16), .dataWidth(16), .bus("separate")) ram_1 (
    .addr(in_2), .din(in_3), .data(out_6), .str(in_4), .sel(1'b1), .clk(in_1), .ld(not_1_out), .clr(in_5));
endmodule

module tc7 (
  input  CLK_IN,
  input  [15:0] in_2,
  input  ENBL,
  input  RESET,
  output [6:0] DATA_OUT,
  output CLK_OUT,
  output ENBL_2,
  output CLEAR
);

  wire and_1_out, and_2_out;

  or or_1 (CLEAR, and_1_out, RESET);
  and and_1 (and_1_out, CLK_IN, and_2_out);
  and and_2 (and_2_out, in_2[7], ENBL);

  assign CLK_OUT = CLK_IN;
  assign DATA_OUT = in_2[6:0];
  assign ENBL_2 = ENBL;

  // Notes on the sheet:
  //   DATA IN
endmodule

module romdrv (
  input  [15:0] ADDR_IN_OUT,
  input  [15:0] DATA_OUT_IN,
  output [15:0] out_3,
  output [15:0] out_4,
  output out_5
);


  assign out_3 = ADDR_IN_OUT;
  assign out_4 = DATA_OUT_IN;
  assign out_5 = 1'b1;
endmodule

module panel (
  input  in_1,
  input  in_2,
  input  in_3,
  input  in_4,
  input  in_5,
  input  in_6,
  input  in_7,
  output out_8,
  output out_9,
  output out_10,
  output out_11,
  output out_12,
  output out_13,
  output out_14
);

  and and_1 (out_10, out_9, in_6);
  D_Flip_Flop d_ff_1 (.clk(in_7), .D(in_5), .Q(out_11));  // open: Qn, preset, en, reset
  D_Flip_Flop d_ff_2 (.clk(in_7), .D(in_4), .Q(out_9));  // open: Qn, preset, en, reset

  assign out_8 = in_6;
  assign out_12 = in_1;
  assign out_13 = in_2;
  assign out_14 = in_3;
endmodule

module cpu_1602 (
  input  [15:0] in_1,
  input  RST,
  input  [15:0] in_3,
  input  CLK,
  input  [15:0] pgm_address,
  output IO_SE,
  output out_7,
  output [15:0] out_8,
  output [15:0] out_9,
  output [15:0] out_10,
  output [15:0] out_11,
  output out_12,
  output out_13,
  output [15:0] stack_load,
  output pgm_data,
  output [7:0] stack_store
);

  wire and_1_out, flowctl_1_store_enable, if_id_1_call, if_id_1_jump, if_id_1_out_13, if_id_1_ret,
       if_id_1_store_enable, storedmx_1_out_11, storedmx_1_out_12, storedmx_1_out_13, storedmx_1_out_14,
       storedmx_1_out_15, storedmx_1_out_16, storedmx_1_out_17, storedmx_1_out_18;
  wire [3:0] if_id_1_dst_sel, if_id_1_src_sel;
  wire [4:0] if_id_1_instr_sel;
  wire [7:0] flags_1_out_5, if_id_1_out_10;
  wire [15:0] arithmetics_1_out_9, arithmetics_1_out_10, arithmetics_1_out_11, arithmetics_1_out_12,
       arithmetics_1_out_13, arithmetics_1_out_14, arithmetics_1_out_15, boolean_1_out_8, boolean_1_out_9,
       boolean_1_out_10, boolean_1_out_11, bus_1_out_48, bus_1_out_49, bus_1_out_50, bus_1_out_51,
       bus_1_out_52, bus_1_out_53, bus_1_out_54, bus_1_out_55, bus_1_out_64, bus_1_out_65, bus_1_out_66,
       bus_1_out_67, bus_1_out_69, bus_1_out_70, bus_1_out_71, bus_1_out_72, bus_1_out_73, bus_1_out_74,
       bus_1_out_75, bus_1_out_76, bus_1_out_77, bus_1_out_78, bus_1_out_79, bus_1_out_80, bus_1_out_81,
       bus_1_out_83, bus_1_out_84, bus_1_out_88, counters_1_out_5, counters_1_out_6, counters_1_out_7,
       counters_1_out_8, flagsmux_1_out_9, flowctl_1_out_10, instr_cmp_1_out_3, instr_copy_1_out_3,
       instr_lflg_1_out_4, instr_load_1_out_2, reg_1_data_out, reg_3_data_out, reg_4_data_out,
       reg_5_data_out, reg_6_data_out, reg_7_data_out, reg_8_data_out;

  and and_1 (and_1_out, CLK, out_12);
  \reg  reg_1 (.in_1(bus_1_out_52), .DATA_OUT(reg_1_data_out), .ENBL(storedmx_1_out_11), .CLK(and_1_out), .RST(RST));
  instr_load instr_load_1 (.out_2(instr_load_1_out_2), .in_1(pgm_address));
  R16C r16c_1 (
    .in_1(flowctl_1_out_10), .out_5(out_11), .RESET(RST), .CLOCK(and_1_out), .UPDATE(flowctl_1_store_enable));
  \reg  reg_2 (.in_1(bus_1_out_53), .DATA_OUT(out_8), .ENBL(storedmx_1_out_12), .CLK(and_1_out), .RST(RST));
  \reg  reg_3 (.in_1(bus_1_out_54), .DATA_OUT(reg_3_data_out), .ENBL(storedmx_1_out_13), .CLK(and_1_out), .RST(RST));
  bus bus_1 (
    .SRC_SELECT(if_id_1_src_sel), .DST_SELECT(if_id_1_dst_sel), .in_9(reg_5_data_out),
    .in_13(reg_1_data_out), .in_10(reg_6_data_out), .in_14(out_8), .in_3(in_1), .in_11(reg_7_data_out),
    .in_15(reg_3_data_out), .in_12(reg_8_data_out), .in_16(reg_4_data_out), .out_48(bus_1_out_48),
    .out_52(bus_1_out_52), .out_49(bus_1_out_49), .out_53(bus_1_out_53), .out_42(out_9),
    .out_50(bus_1_out_50), .out_54(bus_1_out_54), .out_43(out_10), .out_51(bus_1_out_51),
    .out_55(bus_1_out_55), .out_64(bus_1_out_64), .out_72(bus_1_out_72), .out_80(bus_1_out_80),
    .out_88(bus_1_out_88), .out_65(bus_1_out_65), .out_73(bus_1_out_73), .out_81(bus_1_out_81),
    .out_66(bus_1_out_66), .out_74(bus_1_out_74), .out_67(bus_1_out_67), .out_75(bus_1_out_75),
    .out_83(bus_1_out_83), .out_76(bus_1_out_76), .out_84(bus_1_out_84), .out_69(bus_1_out_69),
    .out_77(bus_1_out_77), .out_70(bus_1_out_70), .out_78(bus_1_out_78), .out_71(bus_1_out_71),
    .out_79(bus_1_out_79), .in_20(instr_load_1_out_2), .in_24(instr_copy_1_out_3),
    .in_28(arithmetics_1_out_11), .in_32(boolean_1_out_10), .in_36(counters_1_out_6),
    .in_29(arithmetics_1_out_12), .in_33(boolean_1_out_11), .in_26(arithmetics_1_out_9),
    .in_30(boolean_1_out_8), .in_34(instr_lflg_1_out_4), .in_27(arithmetics_1_out_10),
    .in_31(boolean_1_out_9), .in_35(counters_1_out_5), .in_19(if_id_1_instr_sel));  // open: in_1, in_5, in_2, in_6, in_7, in_4, in_8, out_40, out_44, out_41, out_45, out_46, out_47, out_56, out_57, out_89, out_58, out_82, out_90, out_59, out_91, out_60, out_68, out_92, out_61, out_85, out_93, out_62, out_86, out_94, out_63, out_87, out_95, in_21, in_25, in_37, in_22, in_38, in_23, in_39
  C8_1602 c8_1602_1 (
    .out_6(stack_store), .CLOCK(and_1_out), .RESET(RST), .DEC(if_id_1_ret), .INC(if_id_1_call),
    .ENBL(flowctl_1_store_enable));
  \reg  reg_4 (.in_1(bus_1_out_55), .DATA_OUT(reg_4_data_out), .ENBL(storedmx_1_out_14), .CLK(and_1_out), .RST(RST));
  \reg  reg_5 (.in_1(bus_1_out_48), .DATA_OUT(reg_5_data_out), .ENBL(storedmx_1_out_15), .CLK(and_1_out), .RST(RST));
  instr_copy instr_copy_1 (.in_1(bus_1_out_64), .out_3(instr_copy_1_out_3));  // open: in_2
  flowctl flowctl_1 (
    .in_1(in_3), .in_8(pgm_address), .out_10(flowctl_1_out_10), .RET(if_id_1_ret), .CALL(if_id_1_call),
    .JUMP(if_id_1_jump), .in_7(out_11), .out_9(stack_load), .in_5(if_id_1_out_10), .in_6(flags_1_out_5),
    .store_enable(flowctl_1_store_enable));
  \reg  reg_6 (.in_1(bus_1_out_49), .DATA_OUT(reg_6_data_out), .ENBL(storedmx_1_out_16), .CLK(and_1_out), .RST(RST));
  \reg  reg_7 (.in_1(bus_1_out_50), .DATA_OUT(reg_7_data_out), .ENBL(storedmx_1_out_17), .CLK(and_1_out), .RST(RST));
  instr_cmp instr_cmp_1 (.out_3(instr_cmp_1_out_3), .in_1(bus_1_out_65), .in_2(bus_1_out_69));
  arithmetics arithmetics_1 (
    .in_1(bus_1_out_66), .in_2(bus_1_out_70), .out_9(arithmetics_1_out_9), .in_3(bus_1_out_67),
    .in_4(bus_1_out_71), .out_10(arithmetics_1_out_10), .in_5(bus_1_out_72), .in_6(bus_1_out_76),
    .out_11(arithmetics_1_out_11), .in_7(bus_1_out_73), .in_8(bus_1_out_77), .out_12(arithmetics_1_out_12),
    .out_13(arithmetics_1_out_13), .out_14(arithmetics_1_out_14), .out_15(arithmetics_1_out_15));
  \reg  reg_8 (.in_1(bus_1_out_51), .DATA_OUT(reg_8_data_out), .ENBL(storedmx_1_out_18), .CLK(and_1_out), .RST(RST));
  IF_ID if_id_1 (
    .CLK(and_1_out), .RST(RST), .in_3(pgm_address), .out_10(if_id_1_out_10), .out_11(out_12),
    .out_12(out_13), .RET(if_id_1_ret), .CALL(if_id_1_call), .JUMP(if_id_1_jump), .dst_sel(if_id_1_dst_sel),
    .src_sel(if_id_1_src_sel), .store_enable(if_id_1_store_enable), .instr_sel(if_id_1_instr_sel),
    .out_13(if_id_1_out_13));
  boolean boolean_1 (
    .in_1(bus_1_out_74), .in_2(bus_1_out_78), .in_3(bus_1_out_75), .in_4(bus_1_out_79), .in_5(bus_1_out_80),
    .in_6(bus_1_out_84), .in_7(bus_1_out_81), .out_8(boolean_1_out_8), .out_9(boolean_1_out_9),
    .out_10(boolean_1_out_10), .out_11(boolean_1_out_11));
  flags flags_1 (.in_1(flagsmux_1_out_9), .in_2(if_id_1_out_13), .in_4(and_1_out), .out_5(flags_1_out_5), .in_3(RST));
  instr_lflg instr_lflg_1 (.out_4(instr_lflg_1_out_4), .in_3(flags_1_out_5));  // open: in_1, in_2
  flagsmux flagsmux_1 (
    .in_7(if_id_1_instr_sel), .in_8(if_id_1_out_13), .in_1(instr_cmp_1_out_3), .in_2(arithmetics_1_out_13),
    .in_3(arithmetics_1_out_14), .in_4(arithmetics_1_out_15), .in_5(counters_1_out_7),
    .in_6(counters_1_out_8), .out_9(flagsmux_1_out_9));
  counters counters_1 (
    .in_1(bus_1_out_83), .out_5(counters_1_out_5), .in_3(bus_1_out_88), .out_6(counters_1_out_6),
    .out_7(counters_1_out_7), .out_8(counters_1_out_8));  // open: in_2, in_4
  and and_2 (pgm_data, flowctl_1_store_enable, if_id_1_call);
  storedmx storedmx_1 (
    .DST_SELECT(if_id_1_dst_sel), .out_11(storedmx_1_out_11), .out_12(storedmx_1_out_12),
    .out_13(storedmx_1_out_13), .out_14(storedmx_1_out_14), .out_15(storedmx_1_out_15),
    .out_16(storedmx_1_out_16), .out_9(IO_SE), .out_17(storedmx_1_out_17), .out_10(out_7),
    .out_18(storedmx_1_out_18), .in_2(if_id_1_store_enable));  // open: out_3, out_4, out_5, out_6, out_7, out_8

  // Notes on the sheet:
  //   mem address
  //   mem store
  //   mem load
  //   stack store enable
  //   mem SE
  //   IO store
  //   stack address
endmodule

module \reg  (
  input  [15:0] in_1,
  input  ENBL,
  input  CLK,
  input  RST,
  output [15:0] DATA_OUT
);

  Register #(.width(16)) register_1 (.D(in_1), .en(ENBL), .Q(DATA_OUT), .clk(CLK), .clr(RST));

  // Notes on the sheet:
  //   DATA IN
endmodule

module bus (
  input  [15:0] in_1,
  input  [15:0] in_2,
  input  [15:0] in_3,
  input  [15:0] in_4,
  input  [15:0] in_5,
  input  [15:0] in_6,
  input  [15:0] in_7,
  input  [15:0] in_8,
  input  [15:0] in_9,
  input  [15:0] in_10,
  input  [15:0] in_11,
  input  [15:0] in_12,
  input  [15:0] in_13,
  input  [15:0] in_14,
  input  [15:0] in_15,
  input  [15:0] in_16,
  input  [3:0] SRC_SELECT,
  input  [3:0] DST_SELECT,
  input  [4:0] in_19,
  input  [15:0] in_20,
  input  [15:0] in_21,
  input  [15:0] in_22,
  input  [15:0] in_23,
  input  [15:0] in_24,
  input  [15:0] in_25,
  input  [15:0] in_26,
  input  [15:0] in_27,
  input  [15:0] in_28,
  input  [15:0] in_29,
  input  [15:0] in_30,
  input  [15:0] in_31,
  input  [15:0] in_32,
  input  [15:0] in_33,
  input  [15:0] in_34,
  input  [15:0] in_35,
  input  [15:0] in_36,
  input  [15:0] in_37,
  input  [15:0] in_38,
  input  [15:0] in_39,
  output [15:0] out_40,
  output [15:0] out_41,
  output [15:0] out_42,
  output [15:0] out_43,
  output [15:0] out_44,
  output [15:0] out_45,
  output [15:0] out_46,
  output [15:0] out_47,
  output [15:0] out_48,
  output [15:0] out_49,
  output [15:0] out_50,
  output [15:0] out_51,
  output [15:0] out_52,
  output [15:0] out_53,
  output [15:0] out_54,
  output [15:0] out_55,
  output [15:0] out_56,
  output [15:0] out_57,
  output [15:0] out_58,
  output [15:0] out_59,
  output [15:0] out_60,
  output [15:0] out_61,
  output [15:0] out_62,
  output [15:0] out_63,
  output [15:0] out_64,
  output [15:0] out_65,
  output [15:0] out_66,
  output [15:0] out_67,
  output [15:0] out_68,
  output [15:0] out_69,
  output [15:0] out_70,
  output [15:0] out_71,
  output [15:0] out_72,
  output [15:0] out_73,
  output [15:0] out_74,
  output [15:0] out_75,
  output [15:0] out_76,
  output [15:0] out_77,
  output [15:0] out_78,
  output [15:0] out_79,
  output [15:0] out_80,
  output [15:0] out_81,
  output [15:0] out_82,
  output [15:0] out_83,
  output [15:0] out_84,
  output [15:0] out_85,
  output [15:0] out_86,
  output [15:0] out_87,
  output [15:0] out_88,
  output [15:0] out_89,
  output [15:0] out_90,
  output [15:0] out_91,
  output [15:0] out_92,
  output [15:0] out_93,
  output [15:0] out_94,
  output [15:0] out_95
);

  wire [15:0] multiplexer_1_out, multiplexer_2_out, multiplexer_3_out;

  Multiplexer #(.select(4), .width(16), .enable("false")) multiplexer_1 (
    .in0(in_13), .in1(in_14), .in2(in_15), .in3(in_16), .in4(in_9), .in5(in_10), .in6(in_11), .in7(in_12),
    .in8(in_5), .in9(in_6), .in10(in_7), .in11(in_8), .in12(in_1), .in13(in_2), .in14(in_3), .in15(in_4),
    .out(multiplexer_1_out), .sel(SRC_SELECT));
  Demultiplexer #(.select(5), .width(16), .enable("false")) demultiplexer_1 (
    .out0(out_56), .out1(out_57), .out2(out_58), .out3(out_59), .out4(out_64), .out5(out_65), .out6(out_66),
    .out7(out_67), .out8(out_72), .out9(out_73), .out10(out_74), .out11(out_75), .out12(out_80),
    .out13(out_81), .out14(out_82), .out15(out_83), .out16(out_88), .out17(out_89), .out18(out_90),
    .out19(out_91), .in(multiplexer_1_out), .sel(in_19));  // open: out20, out21, out22, out23, out24, out25, out26, out27, out28, out29, out30, out31
  Multiplexer #(.select(4), .width(16), .enable("false")) multiplexer_2 (
    .in0(in_13), .in1(in_14), .in2(in_15), .in3(in_16), .in4(in_9), .in5(in_10), .in6(in_11), .in7(in_12),
    .in8(in_5), .in9(in_6), .in10(in_7), .in11(in_8), .in12(in_1), .in13(in_2), .in14(in_3), .in15(in_4),
    .out(multiplexer_2_out), .sel(DST_SELECT));
  Demultiplexer #(.select(5), .width(16), .enable("false")) demultiplexer_2 (
    .out0(out_60), .out1(out_61), .out2(out_62), .out3(out_63), .out4(out_68), .out5(out_69), .out6(out_70),
    .out7(out_71), .out8(out_76), .out9(out_77), .out10(out_78), .out11(out_79), .out12(out_84),
    .out13(out_85), .out14(out_86), .out15(out_87), .out16(out_92), .out17(out_93), .out18(out_94),
    .out19(out_95), .in(multiplexer_2_out), .sel(in_19));  // open: out20, out21, out22, out23, out24, out25, out26, out27, out28, out29, out30, out31
  Demultiplexer #(.select(4), .width(16), .enable("false")) demultiplexer_3 (
    .out0(out_52), .out1(out_53), .out2(out_54), .out3(out_55), .out4(out_48), .out5(out_49), .out6(out_50),
    .out7(out_51), .out8(out_44), .out9(out_45), .out10(out_46), .out11(out_47), .out12(out_40),
    .out13(out_41), .out14(out_42), .out15(out_43), .in(multiplexer_3_out), .sel(DST_SELECT));
  Multiplexer #(.select(5), .width(16), .enable("false")) multiplexer_3 (
    .in0(in_20), .in1(in_21), .in2(in_22), .in3(in_23), .in4(in_24), .in5(in_25), .in6(in_26), .in7(in_27),
    .in8(in_28), .in9(in_29), .in10(in_30), .in11(in_31), .in12(in_32), .in13(in_33), .in14(in_34),
    .in15(in_35), .in16(in_36), .in17(in_37), .in18(in_38), .in19(in_39), .out(multiplexer_3_out), .sel(in_19));  // open: in20, in21, in22, in23, in24, in25, in26, in27, in28, in29, in30, in31

  // Notes on the sheet:
  //   SRC LOAD - source data inputs
  //   instruction unit select
  //   DST LOAD - destination data inputs
  //   DST STORE - destination data outputs
  //   DST SELECT
endmodule

module storedmx (
  input  [3:0] DST_SELECT,
  input  in_2,
  output out_3,
  output out_4,
  output out_5,
  output out_6,
  output out_7,
  output out_8,
  output out_9,
  output out_10,
  output out_11,
  output out_12,
  output out_13,
  output out_14,
  output out_15,
  output out_16,
  output out_17,
  output out_18
);

  Demultiplexer #(.select(4), .enable("false")) demultiplexer_1 (
    .out0(out_11), .out1(out_12), .out2(out_13), .out3(out_14), .out4(out_15), .out5(out_16), .out6(out_17),
    .out7(out_18), .out8(out_3), .out9(out_4), .out10(out_5), .out11(out_6), .out12(out_7), .out13(out_8),
    .out14(out_9), .out15(out_10), .in(in_2), .sel(DST_SELECT));

  // Notes on the sheet:
  //   SEDMX - store enable flag demultiplexer
  //   SE - enable store flag
endmodule

module R16C (
  input  [15:0] in_1,
  input  RESET,
  input  UPDATE,
  input  CLOCK,
  output [15:0] out_5
);

  wire not_1_out;
  wire [15:0] counter_1_q;

  not not_1 (not_1_out, UPDATE);
  Register #(.width(16), .trigger("falling")) register_1 (
    .D(counter_1_q), .en(1'b1), .Q(out_5), .clk(CLOCK), .clr(RESET));
  Counter #(.width(16), .max('hffff)) counter_1 (
    .load(UPDATE), .D(in_1), .count(not_1_out), .Q(counter_1_q), .clk(CLOCK), .clr(RESET));  // open: carry

  // Notes on the sheet:
  //   16 bit register with incrementing counter
endmodule

module flowctl (
  input  [15:0] in_1,
  input  RET,
  input  CALL,
  input  JUMP,
  input  [7:0] in_5,
  input  [7:0] in_6,
  input  [15:0] in_7,
  input  [15:0] in_8,
  output [15:0] out_9,
  output [15:0] out_10,
  output store_enable
);

  wire and_1_out, and_2_out, and_3_out, nor_1_out, or_1_out, or_2_out;
  wire [7:0] controlled_buffer_3_out, controlled_buffer_4_out;
  wire [15:0] adder_1_out, controlled_buffer_1_out;

  Multiplexer #(.width(16)) multiplexer_1 (.in0(in_8), .in1(in_1), .out(out_10), .sel(RET), .en(or_1_out));
  or or_1 (or_1_out, RET, CALL, JUMP);
  assign controlled_buffer_1_out = CALL ? in_7 : 16'bz;  // Controlled_Buffer controlled_buffer_1
  Adder #(.width(16)) adder_1 (
    .a(controlled_buffer_1_out), .b({16{1'b0}}), .out(adder_1_out), .cin(1'b1));  // open: cout
  assign out_9 = CALL ? adder_1_out : 16'bz;  // Controlled_Buffer controlled_buffer_2
  assign controlled_buffer_3_out = or_1_out ? in_5 : 8'bz;  // Controlled_Buffer controlled_buffer_3
  and and_1 (and_1_out, controlled_buffer_4_out[1], ~controlled_buffer_4_out[2], controlled_buffer_3_out[2]);  // AND_Gate
  assign controlled_buffer_4_out = or_1_out ? in_6 : 8'bz;  // Controlled_Buffer controlled_buffer_4
  and and_2 (and_2_out, controlled_buffer_4_out[1], controlled_buffer_4_out[2], controlled_buffer_3_out[1]);
  and and_3 (and_3_out, ~controlled_buffer_4_out[1], controlled_buffer_3_out[0]);  // AND_Gate
  or or_2 (or_2_out, and_1_out, and_2_out, and_3_out, nor_1_out);
  assign store_enable = or_1_out ? or_2_out : 1'bz;  // Controlled_Buffer controlled_buffer_5
  Pull_Resistor pull_resistor_1 (.node(store_enable));
  nor nor_1 (nor_1_out, controlled_buffer_3_out[2], controlled_buffer_3_out[1], controlled_buffer_3_out[0]);

  // Notes on the sheet:
  //   RET instruction
  //   stack load
  //   CALL & JUMP instructions
  //   address load
  //   instr counter store
  //   stack select
  //   MUX enable
  //   instruction select
  //   CALL instruction
  //   instr counter load
  //   stack store
  //   instr options
  //   JUMP instruction
  //   flags load
endmodule

module arithmetics (
  input  [15:0] in_1,
  input  [15:0] in_2,
  input  [15:0] in_3,
  input  [15:0] in_4,
  input  [15:0] in_5,
  input  [15:0] in_6,
  input  [15:0] in_7,
  input  [15:0] in_8,
  output [15:0] out_9,
  output [15:0] out_10,
  output [15:0] out_11,
  output [15:0] out_12,
  output [15:0] out_13,
  output [15:0] out_14,
  output [15:0] out_15
);

  wire [15:0] multiplier_1_cout;

  Adder #(.width(16)) adder_1 (.a(in_2), .b(in_1), .out(out_9), .cout(out_13[0]));  // open: cin
  not not_1 (out_13[8], out_13[0]);
  Pull_Resistor pull_resistor_1 (.node({out_13[15:9], out_13[7:1]}));
  not not_2 (out_14[8], out_14[0]);
  Pull_Resistor pull_resistor_2 (.node({out_14[15:9], out_14[7:1]}));
  Subtractor #(.width(16)) subtractor_1 (.a(in_4), .b(in_3), .out(out_10), .bout(out_14[0]));  // open: bin
  or or_1 (out_15[0], multiplier_1_cout[15], multiplier_1_cout[14], multiplier_1_cout[13], multiplier_1_cout[12], multiplier_1_cout[11], multiplier_1_cout[10], multiplier_1_cout[9], multiplier_1_cout[8], multiplier_1_cout[7], multiplier_1_cout[6], multiplier_1_cout[5], multiplier_1_cout[4], multiplier_1_cout[3], multiplier_1_cout[2], multiplier_1_cout[1], multiplier_1_cout[0]);
  not not_3 (out_15[8], out_15[0]);
  Pull_Resistor pull_resistor_3 (.node({out_15[15:9], out_15[7:1]}));
  Multiplier #(.width(16)) multiplier_1 (.a(in_6), .b(in_5), .out(out_11), .cout(multiplier_1_cout));  // open: cin
  Divider #(.width(16)) divider_1 (.a(in_8), .b(in_7), .out(out_12));  // open: upper, rem

  // Notes on the sheet:
  //   source load
  //   destination load
  //   flags set/clear
  //   destination store
  //   source load
  //   destination load
  //   flags set/clear
  //   destination store
  //   source load
  //   destination load
  //   destination store
  //   flags set/clear
  //   source load
  //   destination load
  //   destination store
endmodule

module counters (
  input  [15:0] in_1,
  input  [15:0] in_2,
  input  [15:0] in_3,
  input  [15:0] in_4,
  output [15:0] out_5,
  output [15:0] out_6,
  output [15:0] out_7,
  output [15:0] out_8
);

  wire [15:0] pull_resistor_1_node, pull_resistor_3_node;

  Adder #(.width(16)) adder_1 (.a(in_1), .b(pull_resistor_1_node), .out(out_5), .cin(1'b1), .cout(out_7[0]));
  Pull_Resistor pull_resistor_1 (.node(pull_resistor_1_node));
  not not_1 (out_7[8], out_7[0]);
  Pull_Resistor pull_resistor_2 (.node({out_7[15:9], out_7[7:1]}));
  Pull_Resistor pull_resistor_3 (.node(pull_resistor_3_node));
  not not_2 (out_8[8], out_8[0]);
  Pull_Resistor pull_resistor_4 (.node({out_8[15:9], out_8[7:1]}));
  Subtractor #(.width(16)) subtractor_1 (.a(in_3), .b(pull_resistor_3_node), .out(out_6), .bin(1'b1), .bout(out_8[0]));

  // Notes on the sheet:
  //   source load
  //   destination load
  //   flags set/clear
  //   destination store
  //   source load
  //   destination load
  //   flags set/clear
  //   destination store
endmodule

module flags (
  input  [15:0] in_1,
  input  in_2,
  input  in_3,
  input  in_4,
  output [7:0] out_5
);

  wire [7:0] and_1_out, or_1_out;

  assign or_1_out = out_5 | in_1[7:0];  // OR_Gate or_1, 8 bits wide
  assign and_1_out = or_1_out & ~in_1[15:8];  // AND_Gate and_1, 8 bits wide
  Register register_1 (.D(and_1_out), .en(in_2), .Q(out_5), .clk(in_4), .clr(in_3));
endmodule

module IF_ID (
  input  CLK,
  input  RST,
  input  [15:0] in_3,
  output RET,
  output CALL,
  output JUMP,
  output store_enable,
  output [3:0] dst_sel,
  output [3:0] src_sel,
  output [7:0] out_10,
  output out_11,
  output out_12,
  output out_13,
  output [4:0] instr_sel
);

  wire and_4_out, d_ff_1_q, d_ff_1_qn, decoder_1_out2, decoder_1_out3, multiplexer_2_out, multiplexer_3_out,
       multiplexer_4_out, nand_1_out, or_2_out;
  wire [15:0] register_1_q;
  wire [15:13] multiplexer_1_out;

  and and_1 (CALL, d_ff_1_q, decoder_1_out2);
  D_Flip_Flop #(.trigger("falling")) d_ff_1 (
    .clk(CLK), .D(d_ff_1_qn), .Q(d_ff_1_q), .Qn(d_ff_1_qn), .en(or_2_out), .reset(RST));  // open: preset
  Register #(.width(16)) register_1 (.D(in_3), .en(and_4_out), .Q(register_1_q), .clk(CLK), .clr(RST));
  and and_2 (out_11, multiplexer_1_out[15], ~out_12);  // AND_Gate
  or or_1 (out_12, multiplexer_1_out[14], multiplexer_1_out[13], multiplexer_2_out);
  and and_3 (JUMP, d_ff_1_q, decoder_1_out3);
  or or_2 (or_2_out, d_ff_1_q, multiplexer_3_out);
  and and_4 (and_4_out, d_ff_1_qn, multiplexer_3_out);
  Multiplexer #(.width(16), .enable("false")) multiplexer_1 (
    .in0(register_1_q), .in1(in_3), .out({multiplexer_1_out, instr_sel, out_10[7:4], dst_sel}),
    .sel(d_ff_1_qn));
  Multiplexer #(.select(5), .enable("false")) multiplexer_2 (
    .in0(1'b0), .in1(1'b0), .in2(1'b0), .in3(1'b0), .in4(1'b0), .in5(1'b0), .in6(1'b0), .in7(1'b0),
    .in8(1'b0), .in9(1'b0), .in10(1'b0), .in11(1'b0), .in12(1'b0), .in13(1'b0), .in14(1'b0), .in15(1'b0),
    .in16(1'b0), .in17(1'b1), .in18(1'b1), .in19(1'b1), .in20(1'b1), .in21(1'b1), .in22(1'b1), .in23(1'b1),
    .in24(1'b1), .in25(1'b1), .in26(1'b1), .in27(1'b1), .in28(1'b1), .in29(1'b1), .in30(1'b1), .in31(1'b0),
    .out(multiplexer_2_out), .sel(instr_sel));
  nand nand_1 (nand_1_out, d_ff_1_qn, multiplexer_3_out);
  and and_5 (store_enable, nand_1_out, multiplexer_4_out);
  Decoder #(.select(5), .enable("false")) decoder_1 (
    .out1(RET), .out2(decoder_1_out2), .out3(decoder_1_out3), .sel(instr_sel));  // open: out0, out4, out5, out6, out7, out8, out9, out10, out11, out12, out13, out14, out15, out16, out17, out18, out19, out20, out21, out22, out23, out24, out25, out26, out27, out28, out29, out30, out31
  Multiplexer #(.select(5), .enable("false")) multiplexer_3 (
    .in0(1'b1), .in1(1'b0), .in2(1'b1), .in3(1'b1), .in4(1'b0), .in5(1'b0), .in6(1'b0), .in7(1'b0),
    .in8(1'b0), .in9(1'b0), .in10(1'b0), .in11(1'b0), .in12(1'b0), .in13(1'b0), .in14(1'b0), .in15(1'b0),
    .in16(1'b0), .in31(1'b0), .out(multiplexer_3_out), .sel(instr_sel));  // open: in17, in18, in19, in20, in21, in22, in23, in24, in25, in26, in27, in28, in29, in30
  Multiplexer #(.select(5), .enable("false")) multiplexer_4 (
    .in0(1'b1), .in1(1'b0), .in2(1'b0), .in3(1'b0), .in4(1'b1), .in5(1'b0), .in6(1'b1), .in7(1'b1),
    .in8(1'b1), .in9(1'b1), .in10(1'b1), .in11(1'b1), .in12(1'b1), .in13(1'b1), .in14(1'b1), .in15(1'b1),
    .in16(1'b1), .in31(1'b0), .out(multiplexer_4_out), .sel(instr_sel));  // open: in17, in18, in19, in20, in21, in22, in23, in24, in25, in26, in27, in28, in29, in30
  Multiplexer #(.select(5), .enable("false")) multiplexer_5 (
    .in0(1'b0), .in1(1'b0), .in2(1'b0), .in3(1'b0), .in4(1'b0), .in5(1'b1), .in6(1'b1), .in7(1'b1),
    .in8(1'b1), .in9(1'b0), .in10(1'b0), .in11(1'b0), .in12(1'b0), .in13(1'b0), .in14(1'b0), .in15(1'b1),
    .in16(1'b1), .in31(1'b0), .out(out_13), .sel(instr_sel));  // open: in17, in18, in19, in20, in21, in22, in23, in24, in25, in26, in27, in28, in29, in30

  assign out_10[3:0] = dst_sel;
  assign src_sel = out_10[7:4];

  // Notes on the sheet:
  //   pgm data
  //   instruction ready
  //   invalid instruction code
  //   2-cycle flag
  //   dst store enable
  //   flags modify enable
  //   instr sel
endmodule

module flagsmux (
  input  [15:0] in_1,
  input  [15:0] in_2,
  input  [15:0] in_3,
  input  [15:0] in_4,
  input  [15:0] in_5,
  input  [15:0] in_6,
  input  [4:0] in_7,
  input  in_8,
  output [15:0] out_9
);

  Multiplexer #(.select(5), .width(16)) multiplexer_1 (
    .in0({16{1'b0}}), .in1({16{1'b0}}), .in2({16{1'b0}}), .in3({16{1'b0}}), .in4({16{1'b0}}), .in5(in_1),
    .in6(in_2), .in7(in_3), .in8(in_4), .in9({16{1'b0}}), .in10({16{1'b0}}), .in11({16{1'b0}}),
    .in12({16{1'b0}}), .in13({16{1'b0}}), .in14({16{1'b0}}), .in15(in_5), .in16(in_6), .in17({16{1'b0}}),
    .in18({16{1'b0}}), .in19({16{1'b0}}), .in20({16{1'b0}}), .in21({16{1'b0}}), .in22({16{1'b0}}),
    .in23({16{1'b0}}), .in24({16{1'b0}}), .in25({16{1'b0}}), .in26({16{1'b0}}), .in27({16{1'b0}}),
    .in28({16{1'b0}}), .in29({16{1'b0}}), .in30({16{1'b0}}), .in31({16{1'b0}}), .out(out_9), .sel(in_7),
    .en(in_8));
endmodule

module instr_cmp (
  input  [15:0] in_1,
  input  [15:0] in_2,
  output [15:0] out_3
);

  Comparator #(.width(16), .mode("unsigned")) comparator_1 (
    .a(in_2), .b(in_1), .eq(out_3[9]), .lt(out_3[10]));  // open: gt
  not not_1 (out_3[2], out_3[10]);
  not not_2 (out_3[1], out_3[9]);

  assign {out_3[15:11], out_3[8:3], out_3[0]} = {12{1'b0}};
endmodule

module instr_load (
  input  [15:0] in_1,
  output [15:0] out_2
);


  assign out_2 = in_1;
endmodule

module C8_1602 (
  input  CLOCK,
  input  RESET,
  input  DEC,
  input  INC,
  input  ENBL,
  output [7:0] out_6
);

  wire controlled_buffer_1_out, controlled_buffer_2_out, controlled_buffer_3_out, pull_resistor_2_node;
  wire [7:0] counter_1_q, subtractor_1_out;

  assign controlled_buffer_1_out = ENBL ? controlled_buffer_2_out : 1'bz;  // Controlled_Buffer controlled_buffer_1
  assign controlled_buffer_2_out = DEC ? controlled_buffer_3_out : 1'bz;  // Controlled_Buffer controlled_buffer_2
  assign controlled_buffer_3_out = DEC ? DEC : 1'bz;  // Controlled_Buffer controlled_buffer_3
  Pull_Resistor pull_resistor_1 (.node(controlled_buffer_1_out));
  Pull_Resistor pull_resistor_2 (.node(pull_resistor_2_node));
  assign pull_resistor_2_node = ENBL ? controlled_buffer_3_out : 1'bz;  // Controlled_Buffer controlled_buffer_4
  assign controlled_buffer_3_out = INC ? INC : 1'bz;  // Controlled_Buffer controlled_buffer_5
  Counter #(.trigger("falling")) counter_1 (
    .load(controlled_buffer_1_out), .count(pull_resistor_2_node), .Q(counter_1_q), .clk(CLOCK), .clr(RESET));  // open: D, carry
  Multiplexer #(.width(8), .enable("false")) multiplexer_1 (
    .in0(counter_1_q), .in1(subtractor_1_out), .out(out_6), .sel(controlled_buffer_1_out));
  Subtractor subtractor_1 (.a(counter_1_q), .b({8{1'b0}}), .out(subtractor_1_out), .bin(1'b1));  // open: bout
endmodule

module romchip (
  input  [15:0] in_1,
  output [15:0] out_2
);

  ROM #(.addrWidth(16), .dataWidth(16)) rom_1 (.addr(in_1), .data(out_2), .sel(1'b1));
endmodule

module boolean (
  input  [15:0] in_1,
  input  [15:0] in_2,
  input  [15:0] in_3,
  input  [15:0] in_4,
  input  [15:0] in_5,
  input  [15:0] in_6,
  input  [15:0] in_7,
  output [15:0] out_8,
  output [15:0] out_9,
  output [15:0] out_10,
  output [15:0] out_11
);

  assign out_8 = in_1 & in_2;  // AND_Gate and_1, 16 bits wide
  assign out_9 = in_3 | in_4;  // OR_Gate or_1, 16 bits wide
  assign out_10 = in_5 ^ in_6;  // XOR_Gate xor_1, 16 bits wide
  assign out_11 = ~in_7;  // NOT_Gate not_1, 16 bits wide
endmodule
